# Fritzing sketch cr-h130 (saved by Fritzing 0.9.4)
perfboards: 1

parts:
  WeMos_D1_Mini2 = WeMos D1 Mini
  JP3 = Header 6 [part_number=llll package=1x06-smd-female-v2]
  R1 = Resistor [tolerance=±5% resistance=47k package=THT]
  R2 = Resistor [tolerance=±5% resistance=47k package=THT]
  U3 = TRANSISTOR_NPN_2 [package=to-92]
  U4 = TRANSISTOR_NPN_2 [package=to-92]
  R3 = Resistor [tolerance=±5% resistance=100k package=THT]
  R4 = Resistor [tolerance=±5% resistance=1k package=THT]
  R6 = Resistor [tolerance=±5% resistance=47k package=THT]
  U1 = TRANSISTOR_NPN_2 [package=to-92]
  U5 = TRANSISTOR_NPN_2 [package=to-92]
  U6 = TRANSISTOR_NPN_2 [package=to-92]
  R7 = Resistor [tolerance=±5% resistance=1k package=THT]
  R8 = Resistor [tolerance=±5% resistance=100k package=THT]
  R9 = Resistor [tolerance=±5% resistance=100k package=THT]
  R10 = Resistor [tolerance=±5% resistance=10k package=THT]
  U13 = TRANSISTOR_NPN_2 [package=to-92]
  U14 = TRANSISTOR_NPN_2 [package=to-92]
  R21 = Resistor [tolerance=±5% resistance=2.2k package=THT]
  R22 = Resistor [tolerance=±5% resistance=47k package=THT]
  JP5 = Header 6 [part_number=llll package=1x06-smd-female-v2]
  U2 = TRANSISTOR_NPN_2 [package=to-92]
  R23 = Resistor [tolerance=±5% resistance=4.7k package=THT]

nets:
  N1: WeMos_D1_Mini2.3V3, R4.Pin_0, R7.Pin_0
  N2: WeMos_D1_Mini2.5V, JP3.2, JP5.2, JP5.4
  N3: WeMos_D1_Mini2.D0, R10.Pin_0
  N4: WeMos_D1_Mini2.D1, WeMos_D1_Mini2.RX, R21.Pin_0
  N5: WeMos_D1_Mini2.D2, R6.Pin_1
  N6: WeMos_D1_Mini2.D5, U4.E
  N7: WeMos_D1_Mini2.D6, JP5.5
  N8: WeMos_D1_Mini2.D7, R2.Pin_1
  N9: WeMos_D1_Mini2.D8, R1.Pin_1
  N10: WeMos_D1_Mini2.G, JP3.1, U3.E, U1.E, R10.Pin_1, U13.E, U14.E, JP5.6, U2.E, R23.Pin_1
  N11: JP3.3, U3.C
  N12: JP3.4, R3.Pin_0
  N13: JP3.5, R8.Pin_0, U2.C
  N14: JP3.6, U1.C, R9.Pin_0
  N15: R1.Pin_0, U1.B
  N16: R2.Pin_0, U2.B
  N17: U3.B, R6.Pin_0
  N18: U4.C, R4.Pin_1
  N19: U4.B, R3.Pin_1
  N20: U5.C, U6.E
  N21: U5.B, R9.Pin_1
  N22: U6.C, R7.Pin_1
  N23: U6.B, R8.Pin_1
  N24: U13.C, JP5.3
  N25: U13.B, R22.Pin_1
  N26: U14.C, JP5.1
  N27: U14.B, R21.Pin_1

notes:
  +5V
  R-Power
  V-UP
  W-Power
  GND
  V-DN
